# Fritzing sketch Video01_fase03 (saved by Fritzing 0.9.3b)

parts:
  ESP32_-_Back1 = ESP32 - CAM
  Componente1 = Arduino Uno (Rev3)

nets:
  5V: ESP32_-_Back1.5V, Componente1.5V
  N1: ESP32_-_Back1.GPIO0, ESP32_-_Back1.GND#12
  N2: ESP32_-_Back1.GPIO3_/_RX, Componente1.D0/RX
  N3: ESP32_-_Back1.GPIO1_/_TX, Componente1.D1/TX
  N4: ESP32_-_Back1.GND#16, Componente1.GND, Componente1.RESET

custom parts:
  ESP32 - CAM: The ESP32-CAM has a very competitive small-size camera module that can operate independently as a minimum system with a footprint of only 27*40.5*4.5mm and a deep sleep current of up to 6mA.
