# Fritzing sketch Video02_fase03 (saved by Fritzing 0.9.3b)

parts:
  ESP32_-_Back1 = ESP32 - CAM
  Componente1 = FTDI Basic Programmer

nets:
  N1: ESP32_-_Back1.GND#7, Componente1.GND
  N2: ESP32_-_Back1.5V, Componente1.POWER
  N3: ESP32_-_Back1.GPIO0, ESP32_-_Back1.GND#12
  N4: ESP32_-_Back1.GPIO3_/_RX, Componente1.TXO
  N5: ESP32_-_Back1.GPIO1_/_TX, Componente1.RXI

custom parts:
  ESP32 - CAM: The ESP32-CAM has a very competitive small-size camera module that can operate independently as a minimum system with a footprint of only 27*40.5*4.5mm and a deep sleep current of up to 6mA.
